// Logisim project 241210017HalfFullUsingNand.circ as structural Verilog: 1 circuit, main circuit main
module main (
  input  A,
  input  B,
  input  A_2,
  input  B_2,
  input  Cin
);

  wire nand_1_out, nand_2_out, nand_3_out, nand_4_out, nand_5_out, nand_6_out, nand_7_out, nand_8_out,
       nand_9_out, nand_10_out, nand_11_out, nand_12_out, nand_13_out, nand_14_out;

  nand nand_1 (nand_1_out, A, B);
  nand nand_2 (nand_2_out, A_2, B_2);
  nand nand_3 (nand_3_out, A, nand_1_out);
  nand nand_4 (nand_4_out, nand_1_out, B);
  nand nand_5 (nand_5_out, A_2, nand_2_out);
  nand nand_6 (nand_6_out, nand_2_out, B_2);
  nand nand_7 (nand_7_out, nand_1_out, nand_1_out);
  nand nand_8 (nand_8_out, nand_3_out, nand_4_out);
  LED carry (.in(nand_7_out));
  nand nand_9 (nand_9_out, nand_5_out, nand_6_out);
  LED sum (.in(nand_8_out));
  nand nand_10 (nand_10_out, nand_9_out, Cin);
  nand nand_11 (nand_11_out, nand_9_out, nand_10_out);
  nand nand_12 (nand_12_out, nand_10_out, Cin);
  nand nand_13 (nand_13_out, nand_2_out, nand_10_out);
  nand nand_14 (nand_14_out, nand_11_out, nand_12_out);
  LED carry_2 (.in(nand_13_out));
  LED SUM_2 (.in(nand_14_out));
endmodule
