// Logisim project ENCODER241210017.circ as structural Verilog: 1 circuit, main circuit main
// I0
module main (
  input  y7,
  input  y6,
  input  y5,
  input  y4,
  input  y3,
  input  y2,
  input  y1,
  input  y0,
  output A0,
  output A2,
  output A1
);

  or or_1 (A2, y4, y5, y6, y7);
  or or_2 (A1, y3, y6, y7);
  or or_3 (A0, y1, y3, y5, y7);
endmodule
